# Fritzing sketch circuit schematic (saved by Fritzing 1.0.6)
breadboards: 1

parts:
  A1 = XIAO ESP32C3-smd
  U1 = Vibration Motor- ROB-08449 [package=vibe-motor-10mm]
  R1 = Resistor [tolerance=±5% resistance=1k package="2010 [SMD]"]
  Q1 = NPN-Transistor [package="TO92 [THT]"]
  S1 = Round Pushbutton
  D1 = Rectifier Diode [part_number=1N4001 package="Melf DO-213 AB [SMD]"]
  Bat1 = battery_holder_single_18650
  R2 = Resistor [tolerance=±5% resistance=220k package="2010 [SMD]"]
  R3 = Resistor [tolerance=±5% resistance=220k package="2010 [SMD]"]

nets:
  N1: A1.Pin_8, U1.-, R2.Pin_0
  N2: A1.Pin_11, R1.Pin_0, Q1.C, Bat1.+#0, R3.Pin_0
  N3: A1.Pin_12, R1.Pin_1, Bat1.+#1
  N4: A1.Pin_14, S1.leg1
  N5: A1.Pin_16, R2.Pin_1, R3.Pin_1
  N6: A1.Pin_18, S1.leg0
  N7: U1.+, Q1.E, D1.cathode

notes:
  3.3v
  GND
  D10
  D2
  COM
  NO
  D0

custom parts:
  XIAO ESP32C3-smd: Seeed Studio XIAO ESP32C3 adopts new RISC-V architecture, supporting both Wi-Fi and BLE wireless connectivities.
  battery_holder_single_18650: single 18650 battery holder
