# Fritzing sketch wireless vibrating plushie schematic (saved by Fritzing 1.0.6)
breadboards: 1

parts:
  VCC1 = Battery [internal_resistance=0.1Ω]
  BAT1 = Battery Holders [package=battery-aa]  # not connected
  A1 = XIAO ESP32C3-smd
  U1 = Vibration Motor- ROB-08449 [package=vibe-motor-10mm]
  R1 = Resistor [tolerance=±5% resistance=1k package="2010 [SMD]"]
  R2 = Resistor [tolerance=±5% resistance=100 package="2010 [SMD]"]
  Q1 = NPN-Transistor [package="TO92 [THT]"]

nets:
  N1: VCC1.-, A1.Pin_14, Q1.C
  N2: VCC1.+, R2.Pin_1
  N3: A1.Pin_12, R1.Pin_1
  N4: U1.+, Q1.E
  N5: U1.-, R2.Pin_0
  N6: R1.Pin_0, Q1.B

custom parts:
  XIAO ESP32C3-smd: Seeed Studio XIAO ESP32C3 adopts new RISC-V architecture, supporting both Wi-Fi and BLE wireless connectivities.
